// Logisim project bismuth_1.0.circ as structural Verilog: 1 circuit, main circuit main
module main (
  input  in_1,
  input  in_2,
  input  in_3,
  input  in_4,
  input  in_5,
  input  in_6,
  input  in_7,
  output [15:0] out_8,
  output [15:0] out_9
);

  wire clock_1_out, clock_2_out, clock_3_out, clock_4_out;
  wire [7:0] counter_1_q, counter_2_q;
  wire [15:0] adder_1_out, and_1_out, multiplexer_1_out, multiplier_1_out, nor_1_out, or_1_out,
       shifter_1_out, shifter_2_out, subtractor_1_out, xor_1_out;
  wire [42:0] rom_1_data;

  Counter counter_1 (.clr(in_1), .up(in_3), .count(in_5), .clk(clock_1_out), .Q(counter_1_q));  // open: load, D, carry
  Clock clock_1 (.out(clock_1_out));
  Clock clock_2 (.out(clock_2_out));
  Counter counter_2 (.load(in_1), .up(in_6), .count(in_7), .clk(clock_3_out), .Q(counter_2_q));  // open: clr, D, carry
  Clock clock_3 (.out(clock_3_out));
  RAM #(.dataWidth(16)) ram_1 (.addr(counter_1_q), .we(in_2), .oe(in_4), .clk(clock_2_out), .din(out_9));  // open: dout
  ROM #(.dataWidth(43)) rom_1 (.addr(counter_2_q), .data(rom_1_data));
  Multiplexer #(.width(16)) multiplexer_1 (
    .in0(rom_1_data[22:7]), .in1(out_8), .out(multiplexer_1_out), .sel(rom_1_data[2]));
  Shifter #(.shift("lr"), .width(16)) shifter_1 (.in(multiplexer_1_out), .\dist (rom_1_data[6:3]), .out(shifter_1_out));
  Shifter #(.width(16)) shifter_2 (.in(multiplexer_1_out), .\dist (rom_1_data[6:3]), .out(shifter_2_out));
  assign xor_1_out = multiplexer_1_out ^ rom_1_data[38:23];  // XOR_Gate xor_1, 16 bits wide
  assign nor_1_out = ~(multiplexer_1_out | rom_1_data[38:23]);  // NOR_Gate nor_1, 16 bits wide
  assign or_1_out = multiplexer_1_out | rom_1_data[38:23];  // OR_Gate or_1, 16 bits wide
  assign and_1_out = multiplexer_1_out & rom_1_data[38:23];  // AND_Gate and_1, 16 bits wide
  Multiplier #(.width(16)) multiplier_1 (
    .a(multiplexer_1_out), .b(rom_1_data[38:23]), .out(multiplier_1_out));  // open: cin, cout
  Subtractor #(.width(16)) subtractor_1 (
    .a(multiplexer_1_out), .b(rom_1_data[38:23]), .out(subtractor_1_out));  // open: bin, bout
  Adder #(.width(16)) adder_1 (.a(multiplexer_1_out), .b(rom_1_data[38:23]), .out(adder_1_out));  // open: cin, cout
  Multiplexer #(.select(4), .width(16)) multiplexer_2 (
    .in0(adder_1_out), .in1(subtractor_1_out), .in2(multiplier_1_out), .in3(and_1_out), .in4(or_1_out),
    .in5(nor_1_out), .in6(xor_1_out), .in7(shifter_2_out), .in8(shifter_1_out), .out(out_9),
    .sel(rom_1_data[42:39]));  // open: in9, in10, in11, in12, in13, in14, in15
  Clock clock_4 (.out(clock_4_out));
  Register #(.width(16)) register_1 (.D(out_9), .en(rom_1_data[1]), .clk(clock_4_out), .Q(out_8), .clr(rom_1_data[0]));

  // Notes on the sheet:
  //   contents of rom_1 (hex, n*v repeats v):
  //   5000282 186 8000000306 10000000186 18000000606 20000000486 28000000006 30000007f86 38000000016
  //   40000000016 86 80001f8706 2091a007802 355557fff82 10009000202 8032003202
endmodule
